# Fritzing sketch breadboard_layout (saved by Fritzing 0.9.3b)
breadboards: 1

parts:
  Part2 = Adafruit Feather M0 WINC1500 [part_number="Adafruit #3010"]
  Part4 = Adafruit LSM303DLHC Triple-axis Accelerometer+Magnetometer (Compass) [part_number="Adafruit #1120"]
  R1 = Resistor [tolerance=±5% resistance=2.2k package=THT]
  R2 = Resistor [tolerance=±5% resistance=2.2k package=THT]

nets:
  GND: Part2.GND, Part4.GND
  +3V3: Part2.+3V3, Part4.VIN
  N1: Part2.SCL, R2.Pin_0
  N2: Part2.SDA, R1.Pin_0
  N3: Part4.SCL, R2.Pin_1
  N4: Part4.SDA, R1.Pin_1

custom parts:
  Adafruit Feather M0 WINC1500: This is the Adafruit Feather M0 WiFi w/ATWINC1500 - our take on an 'all-in-one' Arduino-compatible + high speed, reliable WiFi with built in USB and battery charging. Its an Adafruit Feather M0 with a WiFi module, ready to rock! Connect your Feather to the Internet with this fine new FCC-certified WiFi module from Atmel. This 802.11bgn-capable WiFi module is the best new thing for networking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
  Adafruit LSM303DLHC Triple-axis Accelerometer+Magnetometer (Compass): He told you "Go West, young maker!" - but you don't know which way is West! Ah, if only you had this triple-axis accelerometer/magnetometer compass module. Inside are two sensors, one is a classic 3-axis accelerometer, which can tell you which direction is down towards the Earth (by measuring gravity). The other is a magnetometer that can sense where the strongest magnetic force is coming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
